// Logisim project ex2.circ as structural Verilog: 1 circuit, main circuit compute_BrUn
module compute_BrUn (
  input  [31:0] INSTRUCTION,
  output BrUn
);

  wire and_1_out, comparator_1_eq;

  Comparator #(.width(7)) comparator_1 (.a(7'b1100011), .b(INSTRUCTION[6:0]), .eq(comparator_1_eq));  // open: gt, lt
  and and_1 (and_1_out, INSTRUCTION[13], 1'b1);
  and and_2 (BrUn, comparator_1_eq, and_1_out);
endmodule
