// Logisim project control-logic.circ as structural Verilog: 1 circuit, main circuit control_logic
module control_logic (
  input  [31:0] Instruction,
  input  BrEq,
  input  BrLt,
  output PCSel,
  output RegWEn,
  output [2:0] ImmSel,
  output BrUn,
  output ASel,
  output BSel,
  output [3:0] ALUSel,
  output MemWEn,
  output [1:0] WBSel
);

  wire and_1_out, and_2_out, and_3_out, and_4_out, and_5_out, and_6_out, and_7_out, and_8_out, and_9_out,
       and_10_out, and_11_out, and_12_out, and_13_out, and_14_out, and_15_out, and_16_out, and_17_out,
       and_18_out, and_19_out, and_20_out, and_21_out, and_22_out, and_23_out, and_24_out, and_25_out,
       and_26_out, and_27_out, and_28_out, and_29_out, and_30_out, and_31_out, and_32_out, is_000,
       is_0000000, is_0000001, is_001, is_010, is_011, is_100, is_101, is_110, is_111, is_0100000, is_B,
       is_I0, is_I1, is_I2, is_J, is_R, is_S, is_U1, is_U2, not_1_out, not_2_out, or_1_out, or_2_out,
       or_3_out, priority_encoder_1_en_out;
  wire [5:0] priority_encoder_1_out;
  wire [15:14] rom_1_data;

  Comparator #(.width(7)) comparator_1 (.a(Instruction[6:0]), .b(7'b0110011), .eq(is_R));  // open: gt, lt
  Comparator #(.width(7)) comparator_2 (.a(Instruction[6:0]), .b(7'b0000011), .eq(is_I0));  // open: gt, lt
  Comparator #(.width(7)) comparator_3 (.a(Instruction[6:0]), .b(7'b0010011), .eq(is_I1));  // open: gt, lt
  Comparator #(.width(7)) comparator_4 (.a(Instruction[6:0]), .b(7'b1100111), .eq(is_I2));  // open: gt, lt
  Comparator #(.width(7)) comparator_5 (.a(Instruction[6:0]), .b(7'b0100011), .eq(is_S));  // open: gt, lt
  Comparator #(.width(7)) comparator_6 (.a(Instruction[6:0]), .b(7'b1100011), .eq(is_B));  // open: gt, lt
  Comparator #(.width(7)) comparator_7 (.a(Instruction[6:0]), .b(7'b0010111), .eq(is_U1));  // open: gt, lt
  Comparator #(.width(7)) comparator_8 (.a(Instruction[6:0]), .b(7'b0110111), .eq(is_U2));  // open: gt, lt
  Comparator #(.width(7)) comparator_9 (.a(Instruction[6:0]), .b(7'b1101111), .eq(is_J));  // open: gt, lt
  Comparator #(.width(3)) comparator_10 (.a(Instruction[14:12]), .b(3'b000), .eq(is_000));  // open: gt, lt
  Comparator #(.width(3)) comparator_11 (.a(Instruction[14:12]), .b(3'b001), .eq(is_001));  // open: gt, lt
  Comparator #(.width(3)) comparator_12 (.a(Instruction[14:12]), .b(3'b011), .eq(is_011));  // open: gt, lt
  Comparator #(.width(3)) comparator_13 (.a(Instruction[14:12]), .b(3'b010), .eq(is_010));  // open: gt, lt
  Comparator #(.width(3)) comparator_14 (.a(Instruction[14:12]), .b(3'b100), .eq(is_100));  // open: gt, lt
  Comparator #(.width(3)) comparator_15 (.a(Instruction[14:12]), .b(3'b101), .eq(is_101));  // open: gt, lt
  Comparator #(.width(3)) comparator_16 (.a(Instruction[14:12]), .b(3'b110), .eq(is_110));  // open: gt, lt
  Comparator #(.width(3)) comparator_17 (.a(Instruction[14:12]), .b(3'b111), .eq(is_111));  // open: gt, lt
  Comparator #(.width(7)) comparator_18 (.a(Instruction[31:25]), .b({7{1'b0}}), .eq(is_0000000));  // open: gt, lt
  Comparator #(.width(7)) comparator_19 (.a(Instruction[31:25]), .b(7'b0000001), .eq(is_0000001));  // open: gt, lt
  Comparator #(.width(7)) comparator_20 (.a(Instruction[31:25]), .b(7'b0100000), .eq(is_0100000));  // open: gt, lt
  and and_1 (and_1_out, is_000, is_0000001);
  and and_2 (and_2_out, is_R, is_001);
  and and_3 (and_3_out, is_000, is_0100000);
  and and_4 (and_4_out, is_001, is_0000001);
  and and_5 (and_5_out, is_R, is_100);
  and and_6 (and_6_out, is_101, is_0000000);
  and and_7 (and_7_out, is_101, is_0100000);
  and and_8 (and_8_out, is_R, is_110);
  and and_9 (and_9_out, is_R, is_111);
  and and_10 (and_10_out, is_I0, is_001);
  and and_11 (and_11_out, is_010, is_I0);
  and and_12 (and_12_out, is_I1, is_001);
  and and_13 (and_13_out, is_I1, is_010);
  and and_14 (and_14_out, is_I1, is_100);
  and and_15 (and_15_out, is_I1, is_101);
  and and_16 (and_16_out, and_15_out, is_0100000);
  and and_17 (and_17_out, is_I1, is_110);
  and and_18 (and_18_out, is_I1, is_111);
  and and_19 (and_19_out, is_R, is_011);
  and and_20 (and_20_out, is_R, is_010);
  and and_21 (and_21_out, is_S, is_001);
  and and_22 (and_22_out, is_S, is_010);
  and and_23 (and_23_out, is_001, is_B);
  and and_24 (and_24_out, is_B, is_100);
  and and_25 (and_25_out, is_B, is_101);
  and and_26 (and_26_out, is_B, is_110);
  and and_27 (and_27_out, is_B, is_111);
  Priority_Encoder #(.select_enc(6)) priority_encoder_1 (
    .in0(is_R), .in1(and_1_out), .in2(and_3_out), .in3(and_2_out), .in4(and_4_out), .in5(and_19_out),
    .in6(and_20_out), .in7(and_5_out), .in8(and_6_out), .in9(and_7_out), .in10(and_8_out), .in11(and_9_out),
    .in12(is_I0), .in13(and_10_out), .in14(and_11_out), .in15(is_I1), .in16(and_12_out), .in17(and_13_out),
    .in18(and_14_out), .in19(and_15_out), .in20(and_16_out), .in21(and_17_out), .in22(and_18_out),
    .in23(is_S), .in24(and_21_out), .in25(and_22_out), .in26(is_B), .in27(and_23_out), .in28(and_24_out),
    .in29(and_25_out), .in30(and_26_out), .in31(and_27_out), .in32(is_U1), .in33(is_U2), .in34(is_J),
    .in35(is_I2), .in36(1'b0), .in37(1'b0), .in38(1'b0), .in39(1'b0), .in40(1'b0), .in41(1'b0), .in42(1'b0),
    .in43(1'b0), .in44(1'b0), .in45(1'b0), .in46(1'b0), .in47(1'b0), .in48(1'b0), .in49(1'b0), .in50(1'b0),
    .in51(1'b0), .in52(1'b0), .in53(1'b0), .in54(1'b0), .in55(1'b0), .in56(1'b0), .in57(1'b0), .in58(1'b0),
    .in59(1'b0), .in60(1'b0), .in61(1'b0), .in62(1'b0), .in63(1'b0), .out(priority_encoder_1_out),
    .en_out(priority_encoder_1_en_out), .en_in(1'b1));  // open: gs
  ROM #(.addrWidth(6), .dataWidth(16)) rom_1 (
    .addr(priority_encoder_1_out),
    .data({rom_1_data, WBSel, MemWEn, ALUSel, BSel, ASel, BrUn, ImmSel, RegWEn}));
  or or_1 (or_1_out, is_111, is_101);
  not not_1 (not_1_out, BrLt);
  or or_2 (or_2_out, is_100, is_110);
  not not_2 (not_2_out, BrEq);
  and and_28 (and_28_out, or_1_out, not_1_out);
  and and_29 (and_29_out, BrLt, or_2_out);
  and and_30 (and_30_out, BrEq, is_000);
  and and_31 (and_31_out, is_001, not_2_out);
  or or_3 (or_3_out, and_28_out, and_29_out, and_30_out, and_31_out);
  and and_32 (and_32_out, is_B, or_3_out);
  or or_4 (PCSel, and_32_out, is_I2, is_J);
  // also tied to VCC on the sheet: priority_encoder_1_en_out

  // Other names for the same wires on the sheet: opcode[6:0] = Instruction[6:0]; func3[2:0] = Instruction[14:12];
  //   func7[6:0] = Instruction[31:25]

  // Notes on the sheet:
  //   INPUTS to your circuit
  //   DON'T CHANGE THE LOCATIONS OF THE INPUTS AND OUTPUTS!
  //   OUTPUT from your circuit
  //   contents of rom_1 (hex, n*v repeats v):
  //   1001 1401 1601 1081 1481 1581 1101 1201 1281 1681 1301 1381 41 41 41 1041 10c1 1141 1241 12c1 16c1
  //   1341 13c1 842 842 842 4*64 74 74 1067 1047 2069 2041 0 1001 0 1 1 4*0 1011 0 1 1 4*0 10 0 1 1 4*0
  //   100 0 1
  //   ROM FOR CONTROL LOGIC
  //   This is only if you choose to do the ROM option
  //   Reminder: If using ROM, use combinational logic for PCSel
endmodule
