// Logisim project cpu.circ as structural Verilog: 1 circuit, main circuit cpu
module cpu (
  input  clk,
  input  [31:0] Instruction,
  input  [31:0] MemReadData,
  output [31:0] MemAddress,
  output [31:0] ProgramCounter,
  output [31:0] ra,
  output [31:0] sp,
  output [31:0] t0,
  output [31:0] t1,
  output [31:0] t2,
  output [31:0] s0,
  output [31:0] s1,
  output [31:0] a0,
  output [3:0] MemWriteMask,
  output [31:0] MemWriteData
);

  wire ASel, BrEq, BrLt, BrUn, BSel, MemWEn, PCSel, RegWEn;
  wire [1:0] WBSel;
  wire [2:0] ImmSel;
  wire [3:0] ALUSel;
  wire [31:0] A, A1, adder_1_out, B, B1, B2, DataToReg, Instruction2, multiplexer_1_out, multiplexer_2_out,
       PC, PC_Plus_4, WB;

  Multiplexer #(.width(32)) multiplexer_1 (.in0(adder_1_out), .in1(MemAddress), .out(multiplexer_1_out), .sel(PCSel));
  Register #(.width(32)) u_PC (.D(multiplexer_1_out), .en(1'b1), .clk(clk), .Q(ProgramCounter));  // open: clr
  Multiplexer #(.width(32)) multiplexer_2 (.in0(Instruction), .in1(32'h33), .out(multiplexer_2_out), .sel(PCSel));
  Adder #(.width(32)) adder_1 (.a(ProgramCounter), .b(32'h4), .out(adder_1_out));  // open: cin, cout
  Register #(.width(32)) register_1 (.D(multiplexer_2_out), .en(1'b1), .clk(clk), .Q(Instruction2));  // open: clr
  Register #(.width(32)) register_2 (.D(adder_1_out), .en(1'b1), .clk(clk), .Q(PC_Plus_4));  // open: clr
  Register #(.width(32)) register_3 (.D(ProgramCounter), .en(1'b1), .clk(clk), .Q(PC));  // open: clr
  control_logic control_logic_1 (
    .Instruction(Instruction2), .BrEq(BrEq), .BrLt(BrLt), .PCSel(PCSel), .RegWEn(RegWEn), .ImmSel(ImmSel),
    .BrUn(BrUn), .ASel(ASel), .BSel(BSel), .ALUSel(ALUSel), .MemWEn(MemWEn), .WBSel(WBSel));
  regfile regfile_1 (
    .ReadIndex1(Instruction2[19:15]), .ReadIndex2(Instruction2[24:20]), .WriteIndex(Instruction2[11:7]),
    .WriteData(WB), .RegWEn(RegWEn), .clk(clk), .ra(ra), .sp(sp), .t0(t0), .t1(t1), .t2(t2), .s0(s0),
    .s1(s1), .a0(a0), .ReadData1(A1), .ReadData2(B1));
  imm_gen imm_gen_1 (.Instruction(Instruction2), .ImmSel(ImmSel), .Immediate(B2));
  Multiplexer #(.width(32)) multiplexer_3 (.in0(A1), .in1(PC), .out(A), .sel(ASel));
  Multiplexer #(.width(32)) multiplexer_4 (.in0(B1), .in1(B2), .out(B), .sel(BSel));
  branch_comp branch_comp_1 (.BrData1(A1), .BrData2(B1), .BrUn(BrUn), .BrEq(BrEq), .BrLt(BrLt));
  alu alu_1 (.A(A), .B(B), .ALUSel(ALUSel), .ALUResult(MemAddress));
  partial_store partial_store_1 (
    .Instruction(Instruction2), .MemAddress(MemAddress), .DataFromReg(B1), .MemWEn(MemWEn),
    .MemWriteMask(MemWriteMask), .DataToMem(MemWriteData));
  partial_load partial_load_1 (
    .Instruction(Instruction2), .MemAddress(MemAddress), .DataFromMem(MemReadData), .DataToReg(DataToReg));
  Multiplexer #(.select(2), .width(32)) multiplexer_5 (
    .in0(DataToReg), .in1(MemAddress), .in2(PC_Plus_4), .out(WB), .sel(WBSel));  // open: in3

  // Other names for the same wires on the sheet: ALUResult[31:0] = MemAddress; Instruction1[31:0] = Instruction

  // Notes on the sheet:
  //   add x0 x0 x0
  //   To IMEM
  //   IMEM (do **NOT** move this)
  //   From IMEM
  //   Inputs/Outputs for testing. Do **NOT** move these.
  //   To DMEM
  //   DMEM (do **NOT** move this)
  //   From DMEM
endmodule
