// Logisim project imm-gen.circ as structural Verilog: 1 circuit, main circuit imm_gen
module imm_gen (
  input  [31:0] Instruction,
  input  [2:0] ImmSel,
  output [31:0] Immediate
);

  wire [11:0] multiplexer_1_out;

  Multiplexer #(.select(3), .width(12)) multiplexer_1 (
    .in0(Instruction[31:20]), .out(multiplexer_1_out), .sel(ImmSel));  // open: in1, in2, in3, in4, in5, in6, in7
  assign Immediate = {{20{multiplexer_1_out[11]}}, multiplexer_1_out};  // Bit_Extender bit_extender_1

  // Notes on the sheet:
  //   INPUTS to your circuit
  //   DON'T CHANGE THE LOCATIONS OF THE INPUTS AND OUTPUTS!
  //   OUTPUT from your circuit
endmodule
