// Logisim project partial-store.circ as structural Verilog: 1 circuit, main circuit partial_store
module partial_store (
  input  [31:0] Instruction,
  input  [31:0] MemAddress,
  input  [31:0] DataFromReg,
  input  MemWEn,
  output [3:0] MemWriteMask,
  output [31:0] DataToMem
);

  wire \byte , hw;
  wire [3:0] multiplexer_1_out, multiplexer_4_out, shifter_5_out, shifter_6_out;
  wire [4:0] bit_extender_1_out, bit_extender_2_out, shifter_2_out, shifter_4_out;
  wire [31:0] bit_extender_3_out, bit_extender_4_out, multiplexer_2_out, shifter_1_out, shifter_3_out;

  Comparator #(.width(3)) comparator_1 (.a(Instruction[14:12]), .b(3'b000), .eq(\byte ));  // open: gt, lt
  Comparator #(.width(3)) comparator_2 (.a(Instruction[14:12]), .b(3'b001), .eq(hw));  // open: gt, lt
  assign bit_extender_1_out = {{3{1'b0}}, MemAddress[1:0]};  // Bit_Extender bit_extender_1
  assign bit_extender_2_out = {{4{1'b0}}, MemAddress[1]};  // Bit_Extender bit_extender_2
  assign bit_extender_3_out = {{24{1'b0}}, DataFromReg[7:0]};  // Bit_Extender bit_extender_3
  Shifter #(.width(32)) shifter_1 (.in(bit_extender_3_out), .\dist (shifter_2_out), .out(shifter_1_out));
  Shifter #(.width(5)) shifter_2 (.in(bit_extender_1_out), .\dist (3'b011), .out(shifter_2_out));
  assign bit_extender_4_out = {{16{1'b0}}, DataFromReg[15:0]};  // Bit_Extender bit_extender_4
  Shifter #(.width(32)) shifter_3 (.in(bit_extender_4_out), .\dist (shifter_4_out), .out(shifter_3_out));
  Shifter #(.width(5)) shifter_4 (.in(bit_extender_2_out), .\dist (3'b100), .out(shifter_4_out));
  Shifter #(.width(4)) shifter_5 (.in(4'b0001), .\dist (MemAddress[1:0]), .out(shifter_5_out));
  Shifter #(.width(4)) shifter_6 (.in(4'b0011), .\dist ({MemAddress[1], 1'b0}), .out(shifter_6_out));
  Multiplexer #(.width(4)) multiplexer_1 (.in0(4'b1111), .in1(shifter_5_out), .out(multiplexer_1_out), .sel(\byte ));
  Multiplexer #(.width(32)) multiplexer_2 (
    .in0(DataFromReg), .in1(shifter_1_out), .out(multiplexer_2_out), .sel(\byte ));
  Multiplexer #(.width(4)) multiplexer_3 (.in0(4'b0000), .in1(multiplexer_4_out), .out(MemWriteMask), .sel(MemWEn));
  Multiplexer #(.width(4)) multiplexer_4 (
    .in0(multiplexer_1_out), .in1(shifter_6_out), .out(multiplexer_4_out), .sel(hw));
  Multiplexer #(.width(32)) multiplexer_5 (.in0(multiplexer_2_out), .in1(shifter_3_out), .out(DataToMem), .sel(hw));

  // Other names for the same wires on the sheet: offset[1:0] = MemAddress[1:0]

  // Notes on the sheet:
  //   INPUTS to your circuit
  //   DON'T CHANGE THE LOCATIONS OF THE INPUTS AND OUTPUTS!
  //   OUTPUT from your circuit
endmodule
